# Fritzing sketch 1.0 (saved by Fritzing 1.0.3b)
breadboards: 1

parts:
  A1 = Arduino GIGA R1 WiFi
  J1 = Basic Servo
  part = Solenoid  # not connected
  L298N1 = L298N DC motor driver
  Chirp!_Soil_Moisture_Sensor1 = Chirp! Soil Moisture Sensor v2.7.3
  LED1 = smd LED [color="Red (633nm)" package="0805 [SMD]"]  # not connected

nets:
  VCC: A1.Pin_28, A1.Pin_105, A1.Pin_123, J1.vcc, L298N1.5V, Chirp!_Soil_Moisture_Sensor1.Pin_1
  GND: A1.Pin_30, A1.Pin_88, A1.Pin_146, J1.gnd, L298N1.GND, Chirp!_Soil_Moisture_Sensor1.pin_5
  N1: A1.Pin_32, Chirp!_Soil_Moisture_Sensor1.pin_3
  N2: A1.Pin_134, L298N1.IN1
  N3: A1.Pin_135, L298N1.IN2

custom parts:
  Arduino GIGA R1 WiFi: The Arduino GIGA R1 WiFi is designed for ambitious makers who want to step up their game.
  L298N DC motor driver: 2x DC motor driver with 78M05 positive voltage regulator (7..35 V) L298N: max 46 V, 2 A Set 5 V Enable jumper to enable 5 V regultor (needed for the L298N) and +5 V output at screw terminal or supply external +5 V at screw terminal Set ENA and/or ENB to +5 V to enable motor permanently or supply ENA and/or ENB with PWM signal IN1 and IN2 set rotation directory for motor A (OUT1/OUT2) IN2 and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
