# Fritzing sketch 3.1 (saved by Fritzing 1.0.3b)
breadboards: 1

parts:
  A1 = Arduino GIGA R1 WiFi
  L298N1 = L298N DC motor driver
  Chirp!_Soil_Moisture_Sensor1 = Chirp! Soil Moisture Sensor v2.7.3
  Chirp!_Soil_Moisture_Sensor2 = Chirp! Soil Moisture Sensor v2.7.3
  IC1 = DIP - 8 pins [chip_label=IC package="DIP (Dual Inline) [THT]"]
  IC2 = DIP - 8 pins [chip_label=IC package="DIP (Dual Inline) [THT]"]
  J1 = Basic Servo
  BAT1 = BC9VPC [package=bc9vpc]
  LED1 = LED - 5mm [color="Red (633nm)" current=0.030A package="5 mm [THT]"]
  ZS-042_RTC1 = ZS-042 RTC Module

nets:
  N1: A1.Pin_32, Chirp!_Soil_Moisture_Sensor1.pin_3
  N2: A1.Pin_37, Chirp!_Soil_Moisture_Sensor2.pin_3
  GND: A1.Pin_48, A1.Pin_106, A1.Pin_146, L298N1.GND, Chirp!_Soil_Moisture_Sensor1.pin_5, Chirp!_Soil_Moisture_Sensor2.pin_5, J1.gnd, BAT1.V-, LED1.anode, ZS-042_RTC1.GND
  VCC: A1.Pin_63, A1.Pin_65, A1.Pin_123, L298N1.5V, Chirp!_Soil_Moisture_Sensor1.Pin_1, Chirp!_Soil_Moisture_Sensor2.Pin_1, J1.vcc, ZS-042_RTC1.VCC
  N3: A1.Pin_89, LED1.cathode
  N4: A1.Pin_124, ZS-042_RTC1.SCL
  N5: A1.Pin_125, ZS-042_RTC1.SDA
  N6: A1.Pin_134, L298N1.IN1
  N7: A1.Pin_135, L298N1.IN2
  N8: A1.Pin_136, L298N1.IN3
  N9: A1.Pin_138, L298N1.IN4
  N10: L298N1.OUT1, IC2.pin1
  N11: L298N1.OUT2, IC2.pin2
  N12: L298N1.OUT3, IC1.pin2
  N13: L298N1.OUT4, IC1.pin1
  N14: L298N1.12V, BAT1.V+

custom parts:
  Arduino GIGA R1 WiFi: The Arduino GIGA R1 WiFi is designed for ambitious makers who want to step up their game.
  L298N DC motor driver: 2x DC motor driver with 78M05 positive voltage regulator (7..35 V) L298N: max 46 V, 2 A Set 5 V Enable jumper to enable 5 V regultor (needed for the L298N) and +5 V output at screw terminal or supply external +5 V at screw terminal Set ENA and/or ENB to +5 V to enable motor permanently or supply ENA and/or ENB with PWM signal IN1 and IN2 set rotation directory for motor A (OUT1/OUT2) IN2 and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
  DIP - 8 pins: A DIP stand-in part for whatever IC you want. With 8 pins on a 300mil dual inline package (DIP) footprint.
