# Fritzing sketch ServoTurnPlug (saved by Fritzing 1.0.3b)

parts:
  Part1 = Arduino Uno (Rev3) - ICSP
  J1 = Basic Servo

nets:
  N1: Part1.D9_PWM, J1.pulse
  5V: Part1.5V, J1.vcc
  GND: Part1.GND, J1.gnd
