# Fritzing sketch basicTempRead (saved by Fritzing 1.0.3b)

parts:
  Part1 = Arduino Uno (Rev3) - ICSP
  Grove2 = Grove Temperature Sensor

nets:
  N1: Part1.A0, Grove2.SIG
  5V: Part1.5V, Grove2.VCC
  GND: Part1.GND, Grove2.GND

notes:
  My sensor is also a humidity sensor built in however this is the most similar and the wiring is the same.
