# Fritzing sketch time (saved by Fritzing 1.0.3b)

parts:
  ZS-042_RTC1 = ZS-042 RTC Module
  A1 = Arduino GIGA R1 WiFi

nets:
  N1: ZS-042_RTC1.GND, A1.Pin_146
  N2: ZS-042_RTC1.VCC, A1.Pin_28, A1.Pin_123
  N3: ZS-042_RTC1.SDA, A1.Pin_125
  N4: ZS-042_RTC1.SCL, A1.Pin_124

custom parts:
  Arduino GIGA R1 WiFi: The Arduino GIGA R1 WiFi is designed for ambitious makers who want to step up their game.
